// Digital circuit Processador acho.dig as structural Verilog
module Processador_acho (
  input  clock
);

  wire [1:0] register_1_q;
  wire [15:0] IP_q, multiplexer_1_out, ula16_1_p3, ULAA_q, ULAB_q, undriven_4, undriven_5;
  wire [15:3] undriven, undriven_2, undriven_3;

  Register #(.Bits(16)) IP (.C(clock), .Q(IP_q));  // open: D, en
  Reginaldos reginaldos_1 ();  // open: Leitura1, Leitura2, Escrita, DadosReginaldo, Clock, EscrevReginaldo, SaiReginaldo1, SaiReginaldo2
  Register register_1 (.C(clock), .Q(register_1_q[0]));  // open: D, en
  Multiplexer #(.Selector_Bits(2), .Bits(16)) multiplexer_1 (
    .sel(register_1_q), .in_0({undriven, IP_q[11:9]}), .in_1({undriven_2, IP_q[8:6]}),
    .in_2({undriven_3, IP_q[5:3]}), .out(multiplexer_1_out));  // open: in_3
  Register #(.Bits(16)) ULAA (.D(undriven_4), .C(clock), .Q(ULAA_q));  // open: en
  Register #(.Bits(16)) ULAB (.D(undriven_5), .C(clock), .Q(ULAB_q));  // open: en
  // ULA16 ula16_1: pin names not known; wires that end beside it: ULAA_q, ULAB_q, ula16_1_p3
  Register #(.Bits(16)) ULA_out (.D(ula16_1_p3));  // open: C, en, Q
  // Pins of 3 and 16 bits meet at {undriven_3, IP_q[5:3]}
  // Pins of 3 and 16 bits meet at {undriven_2, IP_q[8:6]}
  // Pins of 3 and 16 bits meet at {undriven, IP_q[11:9]}
  // Pins of 1 and 2 bits meet at register_1_q
endmodule
